# Fritzing sketch PCB (saved by Fritzing 0.7.0b)
breadboards: 1

parts:
  NodeMCU = NodeMCU V1.0
  AC = Screw terminal - 2 pins [package=THT]
  C1 = Ceramic Capacitor [capacitance=100nF package="100 mil [THT, multilayer]"]
  HLK-PM1 = HLK-PM01
  Fuse1 = Fuse with Handler [part_number=Htc-15m]
  S1 = Pushbutton [package=THT]
  J1 = shrouded pin header, 14 pins [form="♂ (shrouded male)"]

nets:
  N1: NodeMCU.D0, J1.pin1, J1.pin14
  N2: NodeMCU.D1, J1.pin2, J1.pin13
  N3: NodeMCU.D2, J1.pin3, J1.pin12
  N4: NodeMCU.D3, S1.leg1
  N5: NodeMCU.D5, J1.pin10
  N6: NodeMCU.D6, J1.pin9
  N7: NodeMCU.D7, J1.pin8
  N8: NodeMCU.GND, HLK-PM1.-Vo, S1.leg0, J1.pin4, J1.pin5, J1.pin6, J1.pin7
  N9: NodeMCU.Vin, HLK-PM1.+Vo, J1.pin11
  N10: AC.pin1, Fuse1.Connector2
  N11: AC.pin2, C1.1, HLK-PM1.AC#1
  N12: C1.0, HLK-PM1.AC#0, Fuse1.Connector1

notes:
  By Thanakrit

custom parts:
  NodeMCU V1.0: ESP8266 based NodeMCU
